# Fritzing sketch fARm (saved by Fritzing 0.9.3b)

parts:
  Arduino_Uno = Arduino Uno (Rev3) - ICSP
  Bluetooth = Bluetooth HC-05 Macho
  Hydrométrie = Soil Moisture Sensor

nets:
  N1: Arduino_Uno.A0, Hydrométrie.SIG
  N2: Arduino_Uno.D0/RX, Bluetooth.TXD
  N3: Arduino_Uno.D1/TX, Bluetooth.RXD
  5V: Arduino_Uno.5V, Bluetooth.VCC
  GND: Arduino_Uno.GND, Bluetooth.GND
